// Logisim project simu.circ as structural Verilog: 2 circuits, main circuit main
module main (
);

  wire ACC_IH, ACC_IL, ACC_O, adder_1_cout, ALU_I, ALU_O, button_2_out, CF, CLK, CLR, DEC_I, MAR_I, MAR_O,
       nor_1_out, not_1_out, not_2_out, or_1_out, or_2_out, or_3_out, PC_I, PC_INC, PC_O, RA_I, RA_O, RAM_I,
       RAM_O, RB_I, RB_O, REFF, RO_I, RO_O, RSTF, SCREEN_CLR, SUB, ZF;
  wire [2:0] counter_2_q;
  wire [3:0] register_7_q, register_7_q_2;
  wire [7:0] adder_1_out, ALU_AIN, ALU_BIN, controlled_buffer_8_out, D_BUS, pull_resistor_3_node, ram_1_data,
       register_2_q, register_3_q, register_6_q, register_9_q, rom_1_data, rom_1_data_2, rom_1_data_3,
       rom_1_data_4;
  wire [7:7] pull_resistor_2_node;
  wire [15:0] A_BUS, counter_1_q, register_4_q;

  DotMatrix #(.matrixcols(8), .matrixrows(1), .dotshape("circle")) dotmatrix_1 (
    .col0(D_BUS[7]), .col1(D_BUS[6]), .col2(D_BUS[5]), .col3(D_BUS[4]), .col4(D_BUS[3]), .col5(D_BUS[2]),
    .col6(D_BUS[1]), .col7(D_BUS[0]));
  DotMatrix #(.matrixcols(8), .matrixrows(1), .dotshape("circle")) dotmatrix_2 (
    .col0(ALU_AIN[7]), .col1(ALU_AIN[6]), .col2(ALU_AIN[5]), .col3(ALU_AIN[4]), .col4(ALU_AIN[3]),
    .col5(ALU_AIN[2]), .col6(ALU_AIN[1]), .col7(ALU_AIN[0]));
  DotMatrix #(.matrixcols(8), .matrixrows(1), .dotshape("circle")) dotmatrix_3 (
    .col0(register_2_q[7]), .col1(register_2_q[6]), .col2(register_2_q[5]), .col3(register_2_q[4]),
    .col4(register_2_q[3]), .col5(register_2_q[2]), .col6(register_2_q[1]), .col7(register_2_q[0]));
  DotMatrix #(.matrixcols(16), .matrixrows(1), .dotshape("circle")) dotmatrix_4 (
    .col0(register_4_q[15]), .col1(register_4_q[14]), .col2(register_4_q[13]), .col3(register_4_q[12]),
    .col4(register_4_q[11]), .col5(register_4_q[10]), .col6(register_4_q[9]), .col7(register_4_q[8]),
    .col8(register_4_q[7]), .col9(register_4_q[6]), .col10(register_4_q[5]), .col11(register_4_q[4]),
    .col12(register_4_q[3]), .col13(register_4_q[2]), .col14(register_4_q[1]), .col15(register_4_q[0]));
  DotMatrix #(.matrixcols(8), .matrixrows(1), .dotshape("circle")) dotmatrix_5 (
    .col0(register_3_q[7]), .col1(register_3_q[6]), .col2(register_3_q[5]), .col3(register_3_q[4]),
    .col4(register_3_q[3]), .col5(register_3_q[2]), .col6(register_3_q[1]), .col7(register_3_q[0]));
  Clock clock_1 (.out(CLK));
  Button button_1 (.out(CLR));
  assign D_BUS = RA_O ? ALU_AIN : 8'bz;  // Controlled_Buffer controlled_buffer_1
  Register register_1 (.D(D_BUS), .en(RA_I), .Q(ALU_AIN), .clk(CLK), .clr(CLR));
  assign D_BUS = RO_O ? register_2_q : 8'bz;  // Controlled_Buffer controlled_buffer_2
  Register register_2 (.D(D_BUS), .en(RO_I), .Q(register_2_q), .clk(CLK), .clr(CLR));
  _7_Segment_Display u_7_segment_display_1 (
    .g(rom_1_data_2[3]), .f(rom_1_data_2[2]), .a(rom_1_data_2[1]), .b(rom_1_data_2[0]), .e(rom_1_data_2[7]),
    .d(rom_1_data_2[6]), .c(rom_1_data_2[5]), .dp(rom_1_data_2[4]));
  _7_Segment_Display u_7_segment_display_2 (
    .g(rom_1_data[3]), .f(rom_1_data[2]), .a(rom_1_data[1]), .b(rom_1_data[0]), .e(rom_1_data[7]),
    .d(rom_1_data[6]), .c(rom_1_data[5]), .dp(rom_1_data[4]));
  assign A_BUS = MAR_O ? register_4_q : 16'bz;  // Controlled_Buffer controlled_buffer_3
  DotMatrix #(.matrixcols(8), .matrixrows(1), .dotshape("circle")) dotmatrix_6 (
    .col0(register_6_q[7]), .col1(register_6_q[6]), .col2(register_6_q[5]), .col3(register_6_q[4]),
    .col4(register_6_q[3]), .col5(register_6_q[2]), .col6(register_6_q[1]), .col7(register_6_q[0]));
  Register register_3 (.D(D_BUS), .en(ACC_IH), .Q(register_3_q), .clk(CLK), .clr(CLR));
  _7_Segment_Display u_7_segment_display_3 (
    .g(rom_1_data_3[3]), .f(rom_1_data_3[2]), .a(rom_1_data_3[1]), .b(rom_1_data_3[0]), .e(rom_1_data_3[7]),
    .d(rom_1_data_3[6]), .c(rom_1_data_3[5]), .dp(rom_1_data_3[4]));
  Register #(.width(16)) register_4 (.D(A_BUS), .en(MAR_I), .Q(register_4_q), .clk(CLK), .clr(CLR));
  LED led_1 (.in(MAR_I));
  LED led_2 (.in(MAR_O));
  LED led_3 (.in(RAM_I));
  LED led_4 (.in(RAM_O));
  DotMatrix #(.matrixcols(8), .matrixrows(1), .dotshape("circle")) dotmatrix_7 (
    .col0(ALU_BIN[7]), .col1(ALU_BIN[6]), .col2(ALU_BIN[5]), .col3(ALU_BIN[4]), .col4(ALU_BIN[3]),
    .col5(ALU_BIN[2]), .col6(ALU_BIN[1]), .col7(ALU_BIN[0]));
  ROM #(.dataWidth(32)) rom_1 (
    .addr(register_2_q), .data({rom_1_data_4, rom_1_data_3, rom_1_data_2, rom_1_data}));  // open: sel
  _7_Segment_Display u_7_segment_display_4 (
    .g(rom_1_data_4[3]), .f(rom_1_data_4[2]), .a(rom_1_data_4[1]), .b(rom_1_data_4[0]), .e(rom_1_data_4[7]),
    .d(rom_1_data_4[6]), .c(rom_1_data_4[5]), .dp(rom_1_data_4[4]));
  assign D_BUS = RB_O ? ALU_BIN : 8'bz;  // Controlled_Buffer controlled_buffer_4
  Register register_5 (.D(D_BUS), .en(RB_I), .Q(ALU_BIN), .clk(CLK), .clr(CLR));
  RAM #(.addrWidth(16)) ram_1 (
    .addr(register_4_q), .data(ram_1_data), .clk(CLK), .ld(not_1_out), .clr(button_2_out));  // open: sel
  Button button_2 (.out(button_2_out));
  not not_1 (not_1_out, RAM_I);
  Register register_6 (.D(D_BUS), .en(ACC_IL), .Q(register_6_q), .clk(CLK), .clr(CLR));
  LED led_5 (.in(ACC_IH));
  LED led_6 (.in(ACC_IL));
  LED led_7 (.in(ACC_O));
  Pull_Resistor pull_resistor_1 (.node(D_BUS[7]));
  TTY #(.rows(16), .cols(50)) tty_1 (.data(D_BUS[6:0]), .clk(CLK), .we(RO_I), .clr(or_1_out));
  assign ram_1_data = RAM_I ? D_BUS : 8'bz;  // Controlled_Buffer controlled_buffer_5
  assign D_BUS = RAM_O ? ram_1_data : 8'bz;  // Controlled_Buffer controlled_buffer_6
  assign A_BUS = ACC_O ? {register_3_q, register_6_q} : 16'bz;  // Controlled_Buffer controlled_buffer_7
  LED led_8 (.in(RA_I));
  LED led_9 (.in(RA_O));
  LED led_10 (.in(RB_I));
  LED led_11 (.in(RB_O));
  assign controlled_buffer_8_out = not_2_out ? ALU_BIN : 8'bz;  // Controlled_Buffer controlled_buffer_8
  assign controlled_buffer_8_out = SUB ? ~ALU_BIN : 8'bz;  // Controlled_Inverter controlled_inverter_1
  not not_2 (not_2_out, SUB);
  or or_1 (or_1_out, SCREEN_CLR, CLR);
  DotMatrix #(.matrixcols(16), .matrixrows(1), .dotshape("circle")) dotmatrix_8 (
    .col0(counter_1_q[15]), .col1(counter_1_q[14]), .col2(counter_1_q[13]), .col3(counter_1_q[12]),
    .col4(counter_1_q[11]), .col5(counter_1_q[10]), .col6(counter_1_q[9]), .col7(counter_1_q[8]),
    .col8(counter_1_q[7]), .col9(counter_1_q[6]), .col10(counter_1_q[5]), .col11(counter_1_q[4]),
    .col12(counter_1_q[3]), .col13(counter_1_q[2]), .col14(counter_1_q[1]), .col15(counter_1_q[0]));
  LED led_12 (.in(ALU_I));
  LED led_13 (.in(ALU_O));
  LED led_14 (.in(SUB));
  Adder adder_1 (.a(ALU_AIN), .b(controlled_buffer_8_out), .out(adder_1_out), .cin(SUB), .cout(adder_1_cout));
  LED led_15 (.in(PC_I));
  LED led_16 (.in(PC_INC));
  LED led_17 (.in(PC_O));
  DotMatrix #(.matrixcols(8), .matrixrows(1), .dotshape("circle")) dotmatrix_9 (
    .col0(register_7_q_2[3]), .col1(register_7_q_2[2]), .col2(register_7_q_2[1]), .col3(register_7_q_2[0]),
    .col4(register_7_q[3]), .col5(register_7_q[2]), .col6(register_7_q[1]), .col7(register_7_q[0]));
  Register register_7 (.D(adder_1_out), .en(ALU_I), .Q({register_7_q_2, register_7_q}), .clk(CLK), .clr(CLR));
  Counter #(.width(16), .max('hffff)) counter_1 (
    .load(PC_I), .D(A_BUS), .count(PC_INC), .Q(counter_1_q), .clk(CLK), .clr(CLR));  // open: carry
  assign A_BUS = PC_O ? counter_1_q : 16'bz;  // Controlled_Buffer controlled_buffer_9
  LED led_18 (.in(RO_I));
  LED led_19 (.in(RO_O));
  LED led_20 (.in(DEC_I));
  assign D_BUS = ALU_O ? {register_7_q_2, register_7_q} : 8'bz;  // Controlled_Buffer controlled_buffer_10
  DotMatrix #(.matrixcols(8), .matrixrows(1), .dotshape("circle")) dotmatrix_10 (
    .col0(register_9_q[7]), .col1(register_9_q[6]), .col2(register_9_q[5]), .col3(register_9_q[4]),
    .col4(register_9_q[3]), .col5(register_9_q[2]), .col6(register_9_q[1]), .col7(register_9_q[0]));
  Pull_Resistor pull_resistor_2 (.node(pull_resistor_2_node[7]));
  Register #(.width(1)) register_8 (.D(adder_1_cout), .en(REFF), .Q(CF), .clk(CLK), .clr(or_3_out));
  Register register_9 (.D(D_BUS), .en(DEC_I), .Q(register_9_q), .clk(CLK), .clr(CLR));
  DotMatrix #(.matrixcols(3), .matrixrows(1), .dotshape("circle")) dotmatrix_11 (
    .col0(counter_2_q[2]), .col1(counter_2_q[1]), .col2(counter_2_q[0]));
  Counter #(.width(3), .max('h7), .trigger("falling")) counter_2 (
    .Q(counter_2_q), .clk(CLK), .clr(or_2_out));  // open: load, D, count, carry
  or or_2 (or_2_out, CLR, 1'b0);
  nor nor_1 (nor_1_out, register_7_q_2[0], register_7_q_2[1], register_7_q_2[2], register_7_q_2[3], register_7_q[0], register_7_q[1], register_7_q[2], register_7_q[3]);
  Register #(.width(1)) register_10 (.D(nor_1_out), .en(REFF), .Q(ZF), .clk(CLK), .clr(or_3_out));
  LED led_21 (.in(CF));
  LED led_22 (.in(ZF));
  Pull_Resistor pull_resistor_3 (.node(pull_resistor_3_node[0]));
  Pull_Resistor pull_resistor_4 (.node(pull_resistor_3_node[1]));
  Pull_Resistor pull_resistor_5 (.node(pull_resistor_3_node[2]));
  Pull_Resistor pull_resistor_6 (.node(pull_resistor_3_node[3]));
  Pull_Resistor pull_resistor_7 (.node(pull_resistor_3_node[4]));
  Pull_Resistor pull_resistor_8 (.node(pull_resistor_3_node[5]));
  Pull_Resistor pull_resistor_9 (.node(pull_resistor_3_node[6]));
  Pull_Resistor pull_resistor_10 (.node(pull_resistor_3_node[7]));
  or or_3 (or_3_out, RSTF, CLR);
  ROM #(.addrWidth(13), .dataWidth(32)) rom_2 (
    .addr({counter_2_q, register_9_q, CF, ZF}),
    .data({pull_resistor_3_node, pull_resistor_2_node[7], REFF, RSTF, SCREEN_CLR, DEC_I, RO_O, RO_I, PC_O, PC_INC, PC_I, SUB, ALU_O, ALU_I, RB_O, RB_I, RA_O, RA_I, ACC_O, ACC_IL, ACC_IH, RAM_O, RAM_I, MAR_O, MAR_I}));  // open: sel

  // Notes on the sheet:
  //   A Register
  //   Output Register
  //   Memory Address Register
  //   Accumulator
  //   Output ROM
  //   contents of rom_1 (hex, n*v repeats v):
  //   e7e7e700 21e7e700 cbe7e700 6be7e700 2de7e700 6ee7e700 eee7e700 23e7e700 efe7e700 6fe7e700 e721e700
  //   2121e700 cb21e700 6b21e700 2d21e700 6e21e700 ee21e700 2321e700 ef21e700 6f21e700 e7cbe700 21cbe700
  //   cbcbe700 6bcbe700 2dcbe700 6ecbe700 eecbe700 23cbe700 efcbe700 6fcbe700 e76be700 216be700 cb6be700
  //   6b6be700 2d6be700 6e6be700 ee6be700 236be700 ef6be700 6f6be700 e72de700 212de700 cb2de700 6b2de700
  //   2d2de700 6e2de700 ee2de700 232de700 ef2de700 6f2de700 e76ee700 216ee700 cb6ee700 6b6ee700 2d6ee700
  //   6e6ee700 ee6ee700 236ee700 ef6ee700 6f6ee700 e7eee700 21eee700 cbeee700 6beee700 2deee700 6eeee700
  //   eeeee700 23eee700 efeee700 6feee700 e723e700 2123e700 cb23e700 6b23e700 2d23e700 6e23e700 ee23e700
  //   2323e700 ef23e700 6f23e700 e7efe700 21efe700 cbefe700 6befe700 2defe700 6eefe700 eeefe700 23efe700
  //   efefe700 6fefe700 e76fe700 216fe700 cb6fe700 6b6fe700 2d6fe700 6e6fe700 ee6fe700 236fe700 ef6fe700
  //   6f6fe700 e7e72100 21e72100 cbe72100 6be72100 2de72100 6ee72100 eee72100 23e72100 efe72100 6fe72100
  //   e7212100 21212100 cb212100 6b212100 2d212100 6e212100 ee212100 23212100 ef212100 6f212100 e7cb2100
  //   21cb2100 cbcb2100 6bcb2100 2dcb2100 6ecb2100 eecb2100 23cb2100 efcb2100 6fcb2100 e76b2100 216b2100
  //   cb6b2100 6b6b2100 2d6b2100 6e6b2100 ee6b2100 236b2100 ef6b2100 6f6b2100 e72d2100 212d2100 cb2d2100
  //   6b2d2100 2d2d2100 6e2d2100 ee2d2100 232d2100 ef2d2100 6f2d2100 e76e2100 216e2100 cb6e2100 6b6e2100
  //   2d6e2100 6e6e2100 ee6e2100 236e2100 ef6e2100 6f6e2100 e7ee2100 21ee2100 cbee2100 6bee2100 2dee2100
  //   6eee2100 eeee2100 23ee2100 efee2100 6fee2100 e7232100 21232100 cb232100 6b232100 2d232100 6e232100
  //   ee232100 23232100 ef232100 6f232100 e7ef2100 21ef2100 cbef2100 6bef2100 2def2100 6eef2100 eeef2100
  //   23ef2100 efef2100 6fef2100 e76f2100 216f2100 cb6f2100 6b6f2100 2d6f2100 6e6f2100 ee6f2100 236f2100
  //   ef6f2100 6f6f2100 e7e7cb00 21e7cb00 cbe7cb00 6be7cb00 2de7cb00 6ee7cb00 eee7cb00 23e7cb00 efe7cb00
  //   6fe7cb00 e721cb00 2121cb00 cb21cb00 6b21cb00 2d21cb00 6e21cb00 ee21cb00 2321cb00 ef21cb00 6f21cb00
  //   e7cbcb00 21cbcb00 cbcbcb00 6bcbcb00 2dcbcb00 6ecbcb00 eecbcb00 23cbcb00 efcbcb00 6fcbcb00 e76bcb00
  //   216bcb00 cb6bcb00 6b6bcb00 2d6bcb00 6e6bcb00 ee6bcb00 236bcb00 ef6bcb00 6f6bcb00 e72dcb00 212dcb00
  //   cb2dcb00 6b2dcb00 2d2dcb00 6e2dcb00 ee2dcb00 232dcb00 ef2dcb00 6f2dcb00 e76ecb00 216ecb00 cb6ecb00
  //   6b6ecb00 2d6ecb00 6e6ecb00
  //   RAM
  //   B Register
  //   Program Counter
  //   ALU
  //   Instruction Register
  //   M-Cycle
  //   CF
  //   ZF
  //   Decoder ROM
  //   contents of rom_2 (hex, n*v repeats v):
  //   4*0 24*10001 4*480 4*20100 4*1080 4*1200 4*21000 4*10001 12*800 4*10001 12*2800 4*10001 0 0 4*10001
  //   0 0 0 10001 0 10001 10001 0 10001 4*0 4*10001 0 4*100000 916*0 24*8018 20*0 4*8018 4*1080 4*1200
  //   4*21000 4*8018 4*1080 4*1200 4*21000 4*8018 0 0 4*8018 0 0 0 8018 0 8018 8018 0 8018 4*0 4*8018
  //   921*0 24*10001 20*0 4*10001 12*0 4*10001 12*0 4*10001 0 0 4*10001 0 0 0 10001 0 10001 10001 0 10001
  //   4*0 4*10001 921*0 24*8028 20*0 4*8028 12*0 4*8028 12*0 4*28 0 0 4*28 0 0 0 28 0 28 28 0 28 4*0 4*28
  //   921*0 24*41 20*0 4*41 12*0 4*2841 12*0 4*4040 8000 8000 4*4040 8000 8000 8000 4040 8000 4040 4040
  //   8000 4040 4*8000 4*4040 8000 920*0 4*88 4*208 4*20008 4*104 4*404 4*40004 20*0 4*1004 12*0 4*1004
  //   16*0 8000 8000 4*0 8000 8000 8000 0 8000 0 0 8000 0 4*8000 4*0 8000 916*0 48*10001 32*410001
  //   4*210001 10001 10001 4*210001 10001 10001 10001 210001 10001 210001 210001 10001 210001 4*10001
  //   4*210001 5*10001 912*0 112*88008
endmodule

module Graphic_Card (
);

  wire button_2_out, CLK, CLR, not_1_out, or_1_out, SYN_SCR, V_DISPLAY, VMAR_CLR, VMEM_CLR;
  wire [6:0] VMEM_BUS;
  wire [8:0] VMAR_BUS;

  Clock clock_1 (.out(CLK));
  Button button_1 (.out(CLR));
  Button button_2 (.out(button_2_out));
  Register #(.width(1)) register_1 (.D(1'b1), .en(button_2_out), .Q(V_DISPLAY), .clk(CLK));  // open: clr
  Counter #(.width(9), .max('h1ff)) counter_1 (
    .D({9{1'b1}}), .count(SYN_SCR), .Q(VMAR_BUS), .clk(CLK), .clr(VMAR_CLR));  // open: load, carry
  LED led_1 (.in(SYN_SCR));
  not not_1 (not_1_out, V_DISPLAY);
  RAM #(.addrWidth(9), .dataWidth(7)) ram_1 (
    .addr(VMAR_BUS), .data(VMEM_BUS), .clk(CLK), .ld(not_1_out), .clr(VMEM_CLR));  // open: sel
  TTY tty_1 (.data(VMEM_BUS), .clk(CLK), .we(V_DISPLAY), .clr(CLR));
  or or_1 (or_1_out, VMAR_BUS[0], VMAR_BUS[1], VMAR_BUS[2], VMAR_BUS[3], VMAR_BUS[4], VMAR_BUS[5], VMAR_BUS[6], VMAR_BUS[7], VMAR_BUS[8]);
  and and_1 (VMEM_CLR, or_1_out, VMAR_CLR);
  nor nor_1 (VMAR_CLR, VMEM_BUS[0], VMEM_BUS[1], VMEM_BUS[2], VMEM_BUS[3], VMEM_BUS[4], VMEM_BUS[5], VMEM_BUS[6]);

  // Notes on the sheet:
  //   LOAD / DISPLAY
  //   VMAR
  //   VMEM
endmodule
